# Fritzing sketch circuito-completo (saved by Fritzing 0.9.3b)
breadboards: 1

parts:
  R1 = Resistor [tolerance=±5% resistance=10k package="0603 [SMD]"]
  R3 = Resistor [tolerance=±5% resistance=10k package="0603 [SMD]"]
  R4 = Resistor [tolerance=±5% resistance=10k package="0603 [SMD]"]
  R5 = Resistor [tolerance=±5% resistance=10k package="0603 [SMD]"]
  R6 = Resistor [tolerance=±5% resistance=10k package="0603 [SMD]"]
  S2 = Pushbutton [package="[THT]"]
  S9 = Pushbutton [package="[THT]"]
  S4 = Pushbutton [package="[THT]"]
  S5 = Pushbutton [package="[THT]"]
  S6 = Pushbutton [package="[THT]"]
  S7 = Pushbutton [package="[THT]"]
  S8 = Pushbutton [package="[THT]"]
  R7 = Resistor [tolerance=±5% resistance=10k package="0603 [SMD]"]
  R8 = Resistor [tolerance=±5% resistance=10k package="0603 [SMD]"]
  Componente1 = Arduino Uno (Rev3)
  U2 = ENCODER_2LED [package=encoder_led_2]
  M2 = Stepper Motor - Bipolar
  Componente5 = EasyDriver_v44
  V2 = AC Power [voltage=5 frequency=60]
  R9 = Resistor [tolerance=±5% resistance=220 package="0402 [SMD]"]
  R10 = Resistor [tolerance=±5% resistance=220 package="0402 [SMD]"]
  R11 = Resistor [tolerance=±5% resistance=220 package="0402 [SMD]"]
  U3 = LCD-16X2 [package=lcd-8x2-kit]
  R12 = Resistor [tolerance=±5% resistance=10k package="0603 [SMD]"]
  S10 = Pushbutton [package="[THT]"]

nets:
  N1: R1.Pin_0, R3.Pin_1, S2.Pin_1, S2.Pin_2
  5V: R1.Pin_1, Componente1.5V, U2.SW, U3.VDD, U3.A
  N2: R3.Pin_0, R5.Pin_1, S9.Pin_1, S9.Pin_2
  N3: R4.Pin_0, S5.Pin_1, S5.Pin_2, R7.Pin_1
  N4: R4.Pin_1, R6.Pin_0, S6.Pin_2
  N5: R5.Pin_0, R6.Pin_1, S4.Pin_1, S4.Pin_2
  GND: S2.Pin_3, S2.Pin_4, S9.Pin_3, S9.Pin_4, S4.Pin_3, S4.Pin_4, S5.Pin_3, S5.Pin_4, S6.Pin_3, S6.Pin_4, S7.Pin_3, S7.Pin_4, S8.Pin_3, S8.Pin_4, Componente1.GND, U2.-, Componente5.GND, U3.VSS, U3.K, S10.Pin_3
  N6: S7.Pin_1, S7.Pin_2, R7.Pin_0, R8.Pin_1
  N7: S8.Pin_1, S8.Pin_2, R8.Pin_0
  N8: Componente1.A1, U3.VO
  N9: Componente1.D8, U3.DB4
  N10: Componente1.D9_PWM, R9.Pin_0
  N11: Componente1.D10_PWM/SS, R11.Pin_0
  N12: Componente1.D11_PWM/MOSI, U3.E
  N13: Componente1.D12/MISO, U3.RS
  N14: Componente1.D13/SCK, R10.Pin_0
  N15: Componente1.D2, U3.DB7
  N16: Componente1.D3_PWM, U3.DB6
  N17: Componente1.D4, U3.DB5
  N18: Componente1.D5_PWM, U2.+G
  N19: Componente1.D6_PWM, U2.+R
  N20: Componente1.D7, R12.Pin_1
  N21: M2.A, Componente5.OUT1A
  N22: M2.C, Componente5.OUT2A
  N23: M2.B, Componente5.OUT1B
  N24: M2.D, Componente5.OUT2B
  N25: Componente5.V+, V2.V+
  N26: Componente5.STEP, R11.Pin_1
  N27: Componente5.DIR, R9.Pin_1
  N28: Componente5.VCC, V2.V-
  N29: Componente5.ENABLE, R10.Pin_1
  N30: R12.Pin_0, S10.Pin_1, S10.Pin_2
