# Fritzing sketch circuito-completo (saved by Fritzing 0.9.3b)
breadboards: 1

parts:
  Componente1 = Arduino Uno (Rev3)
  DS1 = DS18B20 1-Wire Temperature Sensor [part_number=DS18B20]
  T1 = LM35 Temperature Sensor [package="TO92 [THT]"]
  Q1 = NPN-Transistor [package="TO92 [THT]"]
  Q2 = NPN-Transistor [package="TO92 [THT]"]
  Q3 = NPN-Transistor [package="TO92 [THT]"]
  D1 = Zener Diode [part_number=1N4732A breakdown_voltage=3.6V package="Melf DO-213 AB [SMD]"]
  D2 = Zener Diode [part_number=1N4732A breakdown_voltage=3.6V package="Melf DO-213 AB [SMD]"]
  D3 = Zener Diode [part_number=1N4732A breakdown_voltage=3.6V package="Melf DO-213 AB [SMD]"]
  R1 = Resistor [tolerance=±5% resistance=220 package="2512 [SMD]"]
  R2 = Resistor [tolerance=±5% resistance=220 package="2512 [SMD]"]
  R3 = Resistor [tolerance=±5% resistance=220 package="2512 [SMD]"]
  R4 = Resistor [tolerance=±5% resistance=4.7k package="2512 [SMD]"]
  T2 = LM35 Temperature Sensor [package="TO92 [THT]"]

nets:
  N1: Componente1.A0, T2.Vout
  N2: Componente1.A5/SCL, T1.Vout
  N3: Componente1.D9_PWM, R3.Pin_0
  N4: Componente1.D10_PWM/SS, R1.Pin_0
  N5: Componente1.D11_PWM/MOSI, R2.Pin_0
  N6: Componente1.D3_PWM, DS1.DQ, R4.Pin_1
  5V: Componente1.5V, DS1.VDD, T1.+Vs, R4.Pin_0, T2.+Vs
  N7: Componente1.GND, Q1.C, Q2.C, Q3.C
  N8: DS1.GND, Q2.E
  N9: T1.GND, Q1.E
  N10: Q1.B, D2.cathode
  N11: Q2.B, D1.cathode
  N12: Q3.E, T2.GND
  N13: Q3.B, D3.cathode
  N14: D1.anode, R1.Pin_1
  N15: D2.anode, R3.Pin_1
  N16: D3.anode, R2.Pin_1
